# Fritzing sketch Projects (saved by Fritzing 0.9.3b)
breadboards: 1

parts:
  Raspberry_Pi_1 = Raspberry Pi 3 [part_number=RPI-3-V1.2]
  LED1 = LED - 5mm [color="Red (633nm)" package="5 mm [THT]"]
  LED2 = LED - 5mm [color="Yellow (595nm)" package="5 mm [THT]"]
  LED3 = LED - 5mm [color="Green (565nm)" package="5 mm [THT]"]
  S1 = Pushbutton [package="[THT]"]
  S2 = Pushbutton [package="[THT]"]
  S3 = Pushbutton [package="[THT]"]
  R3 = Resistor [tolerance=±5% resistance=330 package=THT]
  R4 = Resistor [tolerance=±5% resistance=330 package=THT]
  R5 = Resistor [tolerance=±5% resistance=330 package=THT]

nets:
  N1: Raspberry_Pi_1.GPIO2, S2.Pin_1, S2.Pin_2
  N2: Raspberry_Pi_1.GPIO3, S1.Pin_1, S1.Pin_2
  N3: Raspberry_Pi_1.GPIO4, S3.Pin_1, S3.Pin_2
  N4: Raspberry_Pi_1.GPIO17, LED1.anode
  N5: Raspberry_Pi_1.GPIO27, LED2.anode
  N6: Raspberry_Pi_1.GPIO22, LED3.anode
  N7: Raspberry_Pi_1.GND, S1.Pin_3, S1.Pin_4, S2.Pin_3, S2.Pin_4, S3.Pin_3, S3.Pin_4, R3.Pin_0, R4.Pin_0, R5.Pin_0
  N8: LED1.cathode, R3.Pin_1
  N9: LED2.cathode, R4.Pin_1
  N10: LED3.cathode, R5.Pin_1
